# Fritzing sketch fritzing (saved by Fritzing 0.9.3b)

parts:
  Componente1 = Arduino Uno (Rev3) - ICSP
  R1 = Rotary Potentiometer (Small) [maximum_resistance=100kΩ package=THT]

nets:
  N1: Componente1.A2, R1.wiper
  N2: Componente1.5V, R1.leg1
  N3: Componente1.GND, R1.leg2
